# Fritzing sketch Component Sketch (saved by Fritzing 0.9.3b)
circuit board: 8.46667cm x 5.64444cm

parts:
  Primary_Microcontroller = Adafruit Feather M0 Express [part_number="Adafruit #3403"]
  Part1 = NRF24L01+ Breakout Board
  C1 = Electrolytic Capacitor [capacitance=10µF package="0405 [SMD, electrolytic]"]
  part = Adafruit FXOS8700 + FXAS21002 9 DoF Breakout [part_number="Adafruit #3463"]
  part_2 = Lithium Ion Polymer Battery 3.7v 2500mAh [part_number=328]

nets:
  GND: Primary_Microcontroller.GND, Part1.GND, C1.-, part.GND, part_2.negative
  N1: Primary_Microcontroller.MISO, Part1.MISO
  N2: Primary_Microcontroller.MOSI, Part1.MOSI
  N3: Primary_Microcontroller.SCK, Part1.SCK
  +3V3: Primary_Microcontroller.+3V3, Part1.VCC, C1.+, part.3.3V
  N4: Primary_Microcontroller.VBAT, part_2.positive
  N5: Primary_Microcontroller.D10, Part1.CE
  N6: Primary_Microcontroller.D9, Part1.CS
  N7: Primary_Microcontroller.SCL, part.SCL
  N8: Primary_Microcontroller.SDA, part.SDA

custom parts:
  Adafruit Feather M0 Express: We love all our Feathers equally, but this Feather is very special. It's our first Feather that is specifically designed for use with CircuitPython! CircuitPython is our beginner-oriented flavor of MicroPython - and as the name hints at, its a small but full-featured version of the popular Python programming language specifically for use with circuitry and electronics. That doesn't mean you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
  Adafruit FXOS8700 + FXAS21002 9 DoF Breakout: The NXP Precision 9DoF breakout combines two of the best motion sensors we've tested here at Adafruit: The FXOS8700 3-Axis accelerometer and magnetometer, and the FXAS21002 3-axis gyroscope. These two sensors combine to make a nice 9-DoF kit, that can be used for motion and orientation sensing. In particular, we think this sensor set is ideal for AHRS-based orientation calculations: the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
  Lithium Ion Polymer Battery 3.7v 2500mAh: Lithium ion polymer (also known as 'lipo' or 'lipoly') batteries are thin, light and powerful. The output ranges from 4.2V when completely charged to 3.7V. This battery has a capacity of 2500mAh for a total of about 10 Wh. The batteries come pre-attached with a genuine 2-pin JST-PH connector as shown and include the necessary protection circuitry.
