# Fritzing sketch Secondary Node (saved by Fritzing 0.9.3b)
circuit board: 8.46667cm x 5.64444cm

parts:
  Primary_Microcontroller = Adafruit Feather M0 Express [part_number="Adafruit #3403"]
  Part1 = NRF24L01+ Breakout Board
  C1 = Electrolytic Capacitor [capacitance=10µF package="0405 [SMD, electrolytic]"]
  Part3 = Lithium Ion Polymer Battery 3.7v 1200mAh [part_number=258]
  J2 = Basic Force Sensing Resistor (FSR) [package=THT]
  J3 = Basic Force Sensing Resistor (FSR) [package=THT]
  R1 = Resistor [tolerance=±5% resistance=3.3k package=THT]
  R2 = Resistor [tolerance=±5% resistance=3.3k package=THT]

nets:
  GND: Primary_Microcontroller.GND, Part1.GND, C1.-
  N1: Primary_Microcontroller.MISO, Part1.MISO
  N2: Primary_Microcontroller.MOSI, Part1.MOSI
  N3: Primary_Microcontroller.SCK, Part1.SCK
  N4: Primary_Microcontroller.A1, J3.pin_0, R2.Pin_0
  N5: Primary_Microcontroller.A0, J2.pin_0, R1.Pin_0
  +3V3: Primary_Microcontroller.+3V3, Part1.VCC, C1.+, J2.pin_1
  N6: Primary_Microcontroller.VBAT, Part3.negative
  N7: Primary_Microcontroller.D10, Part1.CE
  N8: Primary_Microcontroller.D9, Part1.CS
  N9: Part3.positive, R1.Pin_1, R2.Pin_1

custom parts:
  Adafruit Feather M0 Express: We love all our Feathers equally, but this Feather is very special. It's our first Feather that is specifically designed for use with CircuitPython! CircuitPython is our beginner-oriented flavor of MicroPython - and as the name hints at, its a small but full-featured version of the popular Python programming language specifically for use with circuitry and electronics. That doesn't mean you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
  Lithium Ion Polymer Battery 3.7v 1200mAh: Lithium ion polymer (also known as 'lipo' or 'lipoly') batteries are thin, light and powerful. The output ranges from 4.2V when completely charged to 3.7V. This battery has a capacity of 1200mAh for a total of about 4.5 Wh. The batteries come pre-attached with a genuine 2-pin JST-PH connector as shown and include the necessary protection circuitry.
